// Logisim project checkers.circ as structural Verilog: 4 circuits, main circuit main
module main (
);

  wire clock_1_out, clock_2_out, Manual_Reset_out, reset, rgb_video_1_p1, rgb_video_1_p3, rgb_video_2_p2;
  wire [2:0] X, Y;
  wire [4:0] entrada, rgb_video_2_p4, rgb_video_2_p5;
  wire [23:0] cor;

  // Rv32im #(.SocBusSelection('h00000193B347A4946c3c6c09)) rv32im_1: pin names not known
  Clock clock_1 (.out(clock_1_out));
  // clock_delay clock_delay_1: pin names not known; wires that end beside it: clock_1_out, reset
  // SocBus #(.SocBusIdentifier('h00000193B347A4946c3c6c09)) socbus_1: pin names not known
  // Socmem #(.SocBusSelection('h00000193B347A4946c3c6c09)) memoria: pin names not known
  // SocPio #(.SocBusSelection('h00000193B347A4946c3c6c09), .StartAddress('h460), .direction("outputonly")) reset: pin names not known
  // SocPio #(.SocBusSelection('h00000193B347A4946c3c6c09), .StartAddress('h400), .direction("outputonly"), .width(3)) saida_x: pin names not known; wires that end beside it: reset
  // SocPio #(.SocBusSelection('h00000193B347A4946c3c6c09), .StartAddress('h418), .direction("outputonly"), .width(3)) saida_y: pin names not known; wires that end beside it: reset
  // SocPio #(.SocBusSelection('h00000193B347A4946c3c6c09), .StartAddress('h430), .direction("outputonly"), .width(24)) cor: pin names not known; wires that end beside it: reset, cor[23], cor[22], cor[21], cor[20], cor[19], cor[18], cor[17], cor[16], cor[15], cor[14], cor[13]
  // SocPio #(.SocBusSelection('h00000193B347A4946c3c6c09), .StartAddress('h448), .width(5)) entrada: pin names not known; wires that end beside it: reset, reset
  Button Manual_Reset (.out(Manual_Reset_out));
  joystick_ctrl joystick_ctrl_1 (.Q(entrada[4]), .E(entrada[3]), .A(entrada[2]), .D(entrada[1]));  // open: X, Y
  or or_1 (reset, Manual_Reset_out, rgb_video_1_p1);
  Button OK (.out(entrada[0]));
  Joystick joystick_1 ();  // open: x, y
  // RGB_Video #(.cursor("No Cursor"), .height(8), .scale(8), .width(8)) rgb_video_1: pin names not known; wires that end beside it: rgb_video_1_p1, reset, rgb_video_1_p3, 1'b1, X, Y, cor
  clock_delay clock_delay_2 (.in_1(clock_2_out), .out_2(rgb_video_1_p3));
  Clock clock_2 (.out(clock_2_out));
  // RGB_Video #(.cursor("No Cursor"), .height(32), .scale(8), .width(32)) rgb_video_2: pin names not known; wires that end beside it: reset, rgb_video_2_p2, 1'b1, rgb_video_2_p4, rgb_video_2_p5, cor
  Clock clock_3 (.out(rgb_video_2_p2));
  upscaler upscaler_1 (
    .x_in(X), .y_in(Y), .clock(rgb_video_2_p2), .scale(5'b00011), .x_out(rgb_video_2_p4),
    .y_out(rgb_video_2_p5));
endmodule

module upscaler (
  input  [2:0] x_in,
  input  [2:0] y_in,
  input  clock,
  input  [4:0] scale,
  output [4:0] x_out,
  output [4:0] y_out
);

  wire comparator_1_eq, comparator_1_gt, comparator_2_eq, comparator_2_gt, nor_1_out, or_1_out, or_2_out;
  wire [4:0] adder_1_out, adder_2_out, multiplexer_1_out;

  Multiplexer #(.width(5)) multiplexer_1 (.in0(scale), .in1(5'b00011), .out(multiplexer_1_out), .sel(nor_1_out));
  nor nor_1 (nor_1_out, scale[4], scale[3], scale[2], scale[1], scale[0]);
  Counter #(.max('h1f), .ongoal("load"), .width(5)) counter_1 (
    .load(or_1_out), .D({x_in, 2'b00}), .Q(x_out), .clk(or_2_out));  // open: count, carry, up, clr
  Adder #(.width(5)) adder_1 (.a({x_in, 2'b00}), .b(multiplexer_1_out), .out(adder_1_out));  // open: cin, cout
  Counter #(.max('h1f), .ongoal("load"), .width(5)) counter_2 (
    .load(or_2_out), .D({y_in, 2'b00}), .Q(y_out), .clk(clock));  // open: count, carry, up, clr
  Adder #(.width(5)) adder_2 (.a({y_in, 2'b00}), .b(multiplexer_1_out), .out(adder_2_out));  // open: cin, cout
  or or_1 (or_1_out, comparator_1_gt, comparator_1_eq);
  Comparator #(.mode("unsigned"), .width(5)) comparator_1 (
    .a(x_out), .b(adder_1_out), .gt(comparator_1_gt), .eq(comparator_1_eq));  // open: lt
  or or_2 (or_2_out, comparator_2_gt, comparator_2_eq);
  Comparator #(.mode("unsigned"), .width(5)) comparator_2 (
    .a(y_out), .b(adder_2_out), .gt(comparator_2_gt), .eq(comparator_2_eq));  // open: lt
endmodule

// ctrl
module joystick_ctrl (
  input  [3:0] X,
  input  [3:0] Y,
  output Q,
  output E,
  output A,
  output D
);

  wire and_1_out, and_2_out, comparator_1_gt, comparator_1_lt, comparator_2_gt, comparator_2_lt,
       demultiplexer_1_out0, demultiplexer_1_out1, demultiplexer_2_out0, demultiplexer_2_out1,
       multiplexer_1_out, multiplexer_2_out, multiplexer_3_out, multiplexer_4_out;

  and and_1 (and_1_out, ~X[0], ~X[1], ~X[2]);  // AND_Gate
  Comparator #(.mode("unsigned"), .width(3)) comparator_1 (
    .a(X[2:0]), .b(3'b100), .gt(comparator_1_gt), .lt(comparator_1_lt));  // open: eq
  and and_2 (and_2_out, ~Y[0], ~Y[1], ~Y[2]);  // AND_Gate
  Comparator #(.mode("unsigned"), .width(3)) comparator_2 (
    .a(Y[2:0]), .b(3'b100), .gt(comparator_2_gt), .lt(comparator_2_lt));  // open: eq
  Multiplexer multiplexer_1 (.in0(comparator_1_lt), .in1(comparator_1_gt), .out(multiplexer_1_out), .sel(X[3]));
  Demultiplexer demultiplexer_1 (
    .out0(demultiplexer_1_out0), .out1(demultiplexer_1_out1), .in(multiplexer_2_out), .sel(X[3]));
  Multiplexer multiplexer_2 (.in0(multiplexer_1_out), .in1(1'b0), .out(multiplexer_2_out), .sel(and_1_out));
  Multiplexer multiplexer_3 (.in0(comparator_2_lt), .in1(comparator_2_gt), .out(multiplexer_3_out), .sel(Y[3]));
  Demultiplexer demultiplexer_2 (
    .out0(demultiplexer_2_out0), .out1(demultiplexer_2_out1), .in(multiplexer_4_out), .sel(Y[3]));
  Multiplexer multiplexer_4 (.in0(multiplexer_3_out), .in1(1'b0), .out(multiplexer_4_out), .sel(and_2_out));
  and and_3 (Q, demultiplexer_1_out0, demultiplexer_2_out0);
  and and_4 (E, demultiplexer_1_out1, demultiplexer_2_out0);
  and and_5 (A, demultiplexer_1_out0, demultiplexer_2_out1);
  and and_6 (D, demultiplexer_1_out1, demultiplexer_2_out1);

  // Notes on the sheet:
  //   left
  //   right
  //   up
  //   down
endmodule

// clk
module clock_delay (
  input  in_1,
  output out_2
);

  wire d_ff_1_q, d_ff_1_qn, d_ff_2_q, d_ff_2_qn, d_ff_3_q, d_ff_3_qn, d_ff_4_qn;

  D_Flip_Flop d_ff_1 (.clk(in_1), .D(d_ff_1_qn), .Q(d_ff_1_q), .Qn(d_ff_1_qn));  // open: preset, reset
  D_Flip_Flop d_ff_2 (.clk(d_ff_1_q), .D(d_ff_2_qn), .Q(d_ff_2_q), .Qn(d_ff_2_qn));  // open: preset, reset
  D_Flip_Flop d_ff_3 (.clk(d_ff_2_q), .D(d_ff_3_qn), .Q(d_ff_3_q), .Qn(d_ff_3_qn));  // open: preset, reset
  D_Flip_Flop d_ff_4 (.clk(d_ff_3_q), .D(d_ff_4_qn), .Q(out_2), .Qn(d_ff_4_qn));  // open: preset, reset
endmodule
