// Logisim project checker.circ as structural Verilog: 2 circuits, main circuit main
module main (
  output [3:0] out_1,
  output [3:0] out_2,
  output [6:0] out_3
);

  wire clock_1_out, clock_3_out, clock_4_out, controle_p3, escrever, Manual_Reset_out, reset, rgb_video_1_p8,
       selecionar_out, undriven, undriven_2;
  wire [2:0] X, Y;
  wire [4:0] rgb_video_1_p10, rgb_video_1_p11;
  wire [23:0] cor;

  // Rv32im #(.SocBusSelection('h0000019244B0BF6E62808738)) rv32im_1: pin names not known
  Clock clock_1 (.out(clock_1_out));
  // SocBus #(.SocBusIdentifier('h0000019244B0BF6E62808738)) socbus_1: pin names not known; wires that end beside it: reset, clock_1_out
  // SocPio #(.SocBusSelection('h0000019244B0BF6E62808738), .StartAddress('h430), .direction("outputonly")) reset: pin names not known
  // SocPio #(.SocBusSelection('h0000019244B0BF6E62808738), .StartAddress('h400), .direction("outputonly"), .width(3)) saida_x: pin names not known
  // SocPio #(.SocBusSelection('h0000019244B0BF6E62808738), .StartAddress('h418), .direction("outputonly"), .width(3)) saida_y: pin names not known
  // SocPio #(.SocBusSelection('h0000019244B0BF6E62808738), .StartAddress('h448), .direction("outputonly"), .width(24)) cor: pin names not known; wires that end beside it: cor[23], cor[22], cor[21], cor[20], cor[19], cor[18], cor[17], cor[16], cor[15], cor[14], cor[13]
  // Socmem #(.SocBusSelection('h0000019244B0BF6E62808738)) memoria: pin names not known
  Button Manual_Reset (.out(Manual_Reset_out));
  or or_1 (reset, Manual_Reset_out, controle_p3);
  // SocPio #(.SocBusSelection('h0000019244B0BF6E62808738), .StartAddress('h460), .width(8)) controle: pin names not known; wires that end beside it: X[2], X[1], controle_p3, X[0]
  // RGB_Video #(.height(32), .scale(8), .width(32)) rgb_video_1: pin names not known; wires that end beside it: cor[3], Y[2], cor[2], Y[1], cor[1], Y[0], cor[0], rgb_video_1_p8, 1'b1, rgb_video_1_p10, rgb_video_1_p11, cor
  Clock clock_2 (.out(rgb_video_1_p8));
  upscaler upscaler_1 (.x(X), .y(Y), .x4(rgb_video_1_p10), .y4(rgb_video_1_p11));
  Joystick joystick_1 ();  // open: x, y
  Button selecionar (.out(selecionar_out));
  // SocPio #(.direction("outputonly")) escrever: pin names not known
  Clock clock_3 (.out(clock_3_out));
  Keyboard keyboard_1 (.clk(clock_3_out), .re(undriven), .data(out_3));  // open: clr, avail
  Joystick joystick_2 (.x(out_1), .y(out_2));
  D_Flip_Flop d_ff_1 (.D(undriven_2), .clk(clock_4_out), .Q(escrever));  // open: Qn, preset, reset
  Clock clock_4 (.out(clock_4_out));
endmodule

// 4x
module upscaler (
  input  [2:0] x,
  input  [2:0] y,
  output [4:0] x4,
  output [4:0] y4
);


  assign x4 = {x, 2'b00};
  assign y4 = {y, 2'b00};
endmodule
